# Fritzing sketch Gong (saved by Fritzing 0.9.3b)
circuit board: 8.46667cm x 5.64444cm
breadboards: 1

parts:
  PNP_Transistor = PNP-Transistor [package="TO92 [THT]"]
  LED_of_Button = LED - 5mm [color="Red (633nm)" package="5 mm [THT]"]
  Raspberry_Pi_1 = Raspberry Pi 3 [part_number=RPI-3-V1.2]
  3_Pin_Switch_of_Button = SWITCH_SPDT [package=kps-1290]

nets:
  N1: PNP_Transistor.E, LED_of_Button.cathode
  N2: PNP_Transistor.B, Raspberry_Pi_1.GPIO15
  N3: PNP_Transistor.C, Raspberry_Pi_1.GND
  N4: LED_of_Button.anode, Raspberry_Pi_1.5V
  N5: Raspberry_Pi_1.3v3, 3_Pin_Switch_of_Button.O
  N6: Raspberry_Pi_1.GPIO14, 3_Pin_Switch_of_Button.P

notes:
  Ground
